// Logisim project hw3.circ as structural Verilog: 4 circuits, main circuit 4BitALU
module _1BitFullAdder (
  input  A,
  input  B,
  input  Carry_In,
  output Answer,
  output Carry_Out
);

  wire and_1_out, and_2_out, and_3_out, xor_1_out;

  and and_1 (and_1_out, A, B);
  and and_2 (and_2_out, Carry_In, A);
  and and_3 (and_3_out, B, Carry_In);
  xor xor_1 (xor_1_out, A, B);
  xor xor_2 (Answer, xor_1_out, Carry_In);
  or or_1 (Carry_Out, and_1_out, and_2_out, and_3_out);

  // Notes on the sheet:
  //   Antonio Calabrese
  //   Homework 3
  //   1 Bit Full Adder
endmodule

module _4BitFullAdder (
  input  [3:0] A,
  input  [3:0] B,
  input  Carry_In,
  output [3:0] Output,
  output Carry_Out
);

  wire n1bitfulladder_1_carry_out, n1bitfulladder_2_carry_out, n1bitfulladder_3_carry_out;

  _1BitFullAdder u_1bitfulladder_1 (
    .A(A[0]), .B(B[0]), .Carry_In(Carry_In), .Answer(Output[0]), .Carry_Out(n1bitfulladder_1_carry_out));
  _1BitFullAdder u_1bitfulladder_2 (
    .A(A[1]), .B(B[1]), .Carry_In(n1bitfulladder_1_carry_out), .Answer(Output[1]),
    .Carry_Out(n1bitfulladder_2_carry_out));
  _1BitFullAdder u_1bitfulladder_3 (
    .A(A[2]), .B(B[2]), .Carry_In(n1bitfulladder_2_carry_out), .Answer(Output[2]),
    .Carry_Out(n1bitfulladder_3_carry_out));
  _1BitFullAdder u_1bitfulladder_4 (
    .A(A[3]), .B(B[3]), .Carry_In(n1bitfulladder_3_carry_out), .Answer(Output[3]), .Carry_Out(Carry_Out));

  // Notes on the sheet:
  //   Homework 3
  //   4 Bit Full Adder
endmodule

// XOR A
module _1BitALU (
  input  S0,
  input  S1,
  input  S2,
  input  A,
  input  B,
  output Output
);

  wire ADD_OUT, AND_OUT, Increment_Out, n1bitfulladder_1_carry_out, n1bitfulladder_2_carry_out, Negate_Out,
       not_1_out, not_3_out, Not_A_Out, OR_OUT, SUB_OUT, xor_3_out, XOR_OUT;

  xor xor_1 (XOR_OUT, A, B);
  and and_1 (AND_OUT, A, B);
  xor xor_2 (Increment_Out, A, 1'b1);
  not not_1 (not_1_out, B);
  _1BitFullAdder u_1bitfulladder_1 (
    .A(A), .B(xor_3_out), .Carry_In(1'b0), .Answer(SUB_OUT), .Carry_Out(n1bitfulladder_1_carry_out));
  xor xor_3 (xor_3_out, not_1_out, 1'b1);
  not not_2 (Not_A_Out, A);
  not not_3 (not_3_out, A);
  xor xor_4 (Negate_Out, not_3_out, 1'b1);
  Multiplexer #(.select(3), .disabled(0), .enable("false")) multiplexer_1 (
    .in0(ADD_OUT), .in1(SUB_OUT), .in2(Increment_Out), .in3(Negate_Out), .in4(AND_OUT), .in5(OR_OUT),
    .in6(Not_A_Out), .in7(XOR_OUT), .out(Output), .sel({S2, S1, S0}));
  _1BitFullAdder u_1bitfulladder_2 (
    .A(A), .B(B), .Carry_In(1'b0), .Answer(ADD_OUT), .Carry_Out(n1bitfulladder_2_carry_out));
  or or_1 (OR_OUT, A, B);
  // also tied to GND on the sheet: {n1bitfulladder_1_carry_out, n1bitfulladder_2_carry_out}

  // Other names for the same wires on the sheet: ADD_A = A; AND_A = A; Increment_A = A; Negate_A = A; Not_A = A;
  //   OR_A = A; SUB_A = A; XOR_A = A; ADD_B = B; AND_B = B; OR_B = B; SUB_B = B; XOR_B = B

  // Notes on the sheet:
  //   XOR
  //   AND
  //   Increment
  //   SUB
  //   Antonio Calabrese
  //   Homework 3
  //   1 Bit ALU
  //   NOT
  //   Negate
  //   ADD
  //   S2 | S1 | S0
  //   0 0 0 ADD
  //   0 0 1 SUB
  //   0 1 0 Increment
  //   0 1 1 Negate
  //   1 0 0 AND
  //   1 0 1 OR
  //   1 1 0 NOT
  //   1 1 1 XOR
  //   OR
endmodule

module _4BitALU (
  input  [3:0] A,
  input  [3:0] B,
  input  S2,
  input  S1,
  input  S0,
  output [3:0] Output
);

  wire [3:0] ADD_OUT, AND_OUT, Increment_OUT, n4bitfulladder_2_output, Negate_OUT, not_1_out, not_2_out,
       NOT_OUT, OR_OUT, SUB_OUT, XOR_OUT;

  _4BitFullAdder u_4bitfulladder_1 (
    .A(not_1_out), .B(4'b0001), .Carry_In(1'b0), .Output(Negate_OUT));  // open: Carry_Out
  assign not_1_out = ~A;  // NOT_Gate not_1, 4 bits wide
  _4BitFullAdder u_4bitfulladder_2 (
    .A(not_2_out), .B(4'b0001), .Carry_In(1'b0), .Output(n4bitfulladder_2_output));  // open: Carry_Out
  assign not_2_out = ~B;  // NOT_Gate not_2, 4 bits wide
  assign XOR_OUT = A ^ B;  // XOR_Gate xor_1, 4 bits wide
  assign OR_OUT = A | B;  // OR_Gate or_1, 4 bits wide
  _4BitFullAdder u_4bitfulladder_3 (
    .A(A), .B(n4bitfulladder_2_output), .Carry_In(1'b0), .Output(SUB_OUT));  // open: Carry_Out
  assign NOT_OUT = ~A;  // NOT_Gate not_3, 4 bits wide
  _4BitFullAdder u_4bitfulladder_4 (.A(A), .B(4'b0001), .Carry_In(1'b0), .Output(Increment_OUT));  // open: Carry_Out
  _4BitFullAdder u_4bitfulladder_5 (.A(A), .B(B), .Carry_In(1'b0), .Output(ADD_OUT));  // open: Carry_Out
  assign AND_OUT = A & B;  // AND_Gate and_1, 4 bits wide
  Multiplexer #(.select(3), .width(4), .disabled(0), .enable("false")) multiplexer_1 (
    .in0(ADD_OUT), .in1(SUB_OUT), .in2(Increment_OUT), .in3(Negate_OUT), .in4(AND_OUT), .in5(OR_OUT),
    .in6(NOT_OUT), .in7(XOR_OUT), .out(Output), .sel({S2, S1, S0}));

  // Other names for the same wires on the sheet: ADD_A[3:0] = A; AND_A[3:0] = A; Increment_A[3:0] = A;
  //   Negate_A[3:0] = A; NOT_A[3:0] = A; OR_A[3:0] = A; SUB_A[3:0] = A; XOR_A[3:0] = A; ADD_B[3:0] = B;
  //   AND_B[3:0] = B; OR_B[3:0] = B; SUB_B[3:0] = B; XOR_B[3:0] = B

  // Notes on the sheet:
  //   XOR
  //   OR
  //   Negate
  //   Sub
  //   NOT A
  //   AND
  //   Increment
  //   Add
  //   Antonio Calabrese
  //   Homework 3
  //   4 Bit ALU
  //   S2 | S1 | S0
  //   1 1 1 XOR
  //   1 1 0 NOT
  //   1 0 1 OR
  //   1 0 0 AND
  //   0 1 1 Negate
  //   0 0 1 Sub
  //   0 1 0 Increment
endmodule
