// Logisim project lab4.circ as structural Verilog
module Question1 (
  input  A,
  input  B,
  input  C,
  output Output
);

  wire and_1_out, and_2_out, not_1_out;

  not not_1 (not_1_out, B);
  and and_1 (and_1_out, A, not_1_out);
  and and_2 (and_2_out, B, C);
  or or_1 (Output, and_1_out, and_2_out);

  // Notes on the sheet:
  //   Antonio Calabrese
  //   Question 1
endmodule

module Question2 (
  input  A,
  input  B,
  input  C,
  output Output
);

  wire and_1_out, and_2_out, not_1_out, not_2_out;

  not not_1 (not_1_out, B);
  and and_1 (and_1_out, not_1_out, not_2_out);
  not not_2 (not_2_out, C);
  and and_2 (and_2_out, B, C);
  or or_1 (Output, A, and_1_out, and_2_out);

  // Notes on the sheet:
  //   Antonio Calabrese
  //   Question 2
endmodule

module Question3 (
  input  A,
  input  B,
  input  C,
  input  D,
  output Output
);

  wire and_1_out, and_2_out, and_3_out, and_4_out, not_1_out, not_2_out, not_3_out, not_4_out, not_5_out,
       not_6_out, not_7_out;

  and and_1 (and_1_out, A, not_1_out);
  not not_1 (not_1_out, B);
  not not_2 (not_2_out, B);
  and and_2 (and_2_out, not_2_out, not_3_out);
  not not_3 (not_3_out, D);
  not not_4 (not_4_out, A);
  not not_5 (not_5_out, D);
  and and_3 (and_3_out, not_4_out, not_5_out, C);
  and and_4 (and_4_out, A, B, not_6_out, not_7_out);
  not not_6 (not_6_out, C);
  not not_7 (not_7_out, D);
  or or_1 (Output, and_1_out, and_2_out, and_3_out, and_4_out);

  // Notes on the sheet:
  //   Antonio Calabrese
  //   Question 4
endmodule
