// Logisim project practice.circ as structural Verilog: 1 circuit, main circuit my circuit
module my_circuit (
  input  Address_S0,
  input  Address_S1,
  input  Address_S2,
  input  Data_In_S1,
  input  Data_In_S0,
  input  Write_Enable,
  output [1:0] out_7
);

  wire _000A, _000B, _001A, and_1_out, and_2_out, and_3_out, and_4_out, and_5_out, and_6_out, and_7_out,
       and_8_out, decoder_1_out0, decoder_1_out1, decoder_1_out2, decoder_1_out3, decoder_1_out4,
       decoder_1_out5, decoder_1_out6, decoder_1_out7;

  Decoder #(.select(3), .enable("false")) decoder_1 (
    .out0(decoder_1_out0), .out1(decoder_1_out1), .out2(decoder_1_out2), .out3(decoder_1_out3),
    .out4(decoder_1_out4), .out5(decoder_1_out5), .out6(decoder_1_out6), .out7(decoder_1_out7),
    .sel({Address_S2, Address_S1, Address_S0}));
  and and_1 (and_1_out, decoder_1_out7, Write_Enable);
  and and_2 (and_2_out, decoder_1_out6, Write_Enable);
  and and_3 (and_3_out, decoder_1_out5, Write_Enable);
  and and_4 (and_4_out, decoder_1_out4, Write_Enable);
  and and_5 (and_5_out, decoder_1_out3, Write_Enable);
  and and_6 (and_6_out, decoder_1_out2, Write_Enable);
  and and_7 (and_7_out, decoder_1_out1, Write_Enable);
  and and_8 (and_8_out, decoder_1_out0, Write_Enable);
  D_Flip_Flop #(.trigger("high")) d_ff_1 (.clk(1'b1), .D(Data_In_S1), .en(and_1_out));  // open: Q, Qn, preset, reset
  D_Flip_Flop #(.trigger("high")) d_ff_2 (.clk(1'b1), .D(Data_In_S1), .en(and_3_out));  // open: Q, Qn, preset, reset
  D_Flip_Flop #(.trigger("high")) d_ff_3 (.clk(1'b1), .D(Data_In_S1), .en(and_5_out));  // open: Q, Qn, preset, reset
  D_Flip_Flop #(.trigger("high")) d_ff_4 (
    .clk(1'b1), .D(Data_In_S1), .Qn(_001A), .en(and_7_out));  // open: Q, preset, reset
  Multiplexer #(.select(3), .disabled(0), .enable("false")) multiplexer_1 (
    .in0(_000A), .in1(_001A), .out(out_7[1]), .sel({Address_S2, Address_S1, Address_S0}));  // open: in2, in3, in4, in5, in6, in7
  D_Flip_Flop #(.trigger("high")) d_ff_5 (.clk(1'b1), .D(Data_In_S1), .en(and_2_out));  // open: Q, Qn, preset, reset
  D_Flip_Flop d_ff_6 (.clk(1'b1), .D(Data_In_S1), .en(and_4_out));  // open: Q, Qn, preset, reset
  D_Flip_Flop #(.trigger("high")) d_ff_7 (.clk(1'b1), .D(Data_In_S1), .en(and_6_out));  // open: Q, Qn, preset, reset
  D_Flip_Flop #(.trigger("high")) d_ff_8 (
    .clk(1'b1), .D(Data_In_S1), .Qn(_000A), .en(and_8_out));  // open: Q, preset, reset
  Multiplexer #(.select(3), .disabled(0), .enable("false")) multiplexer_2 (
    .in0(_000B), .out(out_7[0]), .sel({Address_S2, Address_S1, Address_S0}));  // open: in1, in2, in3, in4, in5, in6, in7
  D_Flip_Flop #(.trigger("high")) d_ff_9 (.clk(1'b1), .D(Data_In_S0), .en(and_1_out));  // open: Q, Qn, preset, reset
  D_Flip_Flop #(.trigger("high")) d_ff_10 (.clk(1'b1), .D(Data_In_S0), .en(and_2_out));  // open: Q, Qn, preset, reset
  D_Flip_Flop #(.trigger("high")) d_ff_11 (.clk(1'b1), .D(Data_In_S0), .en(and_3_out));  // open: Q, Qn, preset, reset
  D_Flip_Flop d_ff_12 (.clk(1'b1), .D(Data_In_S0), .en(and_4_out));  // open: Q, Qn, preset, reset
  D_Flip_Flop d_ff_13 (.clk(1'b1), .D(Data_In_S0), .en(and_5_out));  // open: Q, Qn, preset, reset
  D_Flip_Flop d_ff_14 (.clk(1'b1), .D(Data_In_S0), .en(and_6_out));  // open: Q, Qn, preset, reset
  D_Flip_Flop d_ff_15 (.clk(1'b1), .D(Data_In_S0), .en(and_7_out));  // open: Q, Qn, preset, reset
  D_Flip_Flop #(.trigger("high")) d_ff_16 (
    .clk(1'b1), .D(Data_In_S0), .Qn(_000B), .en(and_8_out));  // open: Q, preset, reset

  // Other names for the same wires on the sheet: WriteTunnel = Write_Enable
endmodule
