// Logisim project lab8problem2.circ as structural Verilog: 1 circuit, main circuit my circuit
module my_circuit (
);

  wire and_1_out, and_2_out, and_3_out, and_5_out, and_6_out, and_7_out, and_8_out, and_9_out, and_10_out,
       button_1_out, button_2_out, clock_1_out, not_1_out, not_2_out, not_3_out, not_4_out, not_5_out;
  wire [4:0] or_2_out, register_1_q;

  Register #(.width(5)) register_1 (.D(or_2_out), .Q(register_1_q), .clk(clock_1_out), .clr(button_1_out));  // open: en
  Clock clock_1 (.out(clock_1_out));
  Button button_1 (.out(button_1_out));
  LED led_1 (.in(register_1_q[2]));
  Button button_2 (.out(button_2_out));
  not not_1 (not_1_out, button_2_out);
  not not_2 (not_2_out, button_2_out);
  not not_3 (not_3_out, button_2_out);
  not not_4 (not_4_out, button_2_out);
  not not_5 (not_5_out, button_2_out);
  and and_1 (and_1_out, register_1_q[0], button_2_out);
  and and_2 (and_2_out, not_1_out, register_1_q[1]);
  and and_3 (and_3_out, register_1_q[2], button_2_out);
  and and_4 (or_2_out[3], register_1_q[2], not_2_out);
  and and_5 (and_5_out, register_1_q[3], not_3_out);
  and and_6 (and_6_out, register_1_q[4], not_4_out);
  and and_7 (and_7_out, register_1_q[0], not_5_out);
  and and_8 (and_8_out, ~register_1_q[4], ~register_1_q[3], ~register_1_q[1], ~register_1_q[2], ~register_1_q[0]);  // AND_Gate
  and and_9 (and_9_out, register_1_q[1], button_2_out);
  and and_10 (and_10_out, register_1_q[4], button_2_out);
  or or_1 (or_2_out[2], and_2_out, and_5_out);
  or or_2 (or_2_out[0], and_6_out, and_8_out, and_7_out);
  or or_3 (or_2_out[1], and_1_out, and_9_out);
  or or_4 (or_2_out[4], and_3_out, and_10_out);
endmodule
