// Logisim project lab8problem3.circ as structural Verilog: 1 circuit, main circuit my circuit
module my_circuit (
);

  wire A_out, and_1_out, and_2_out, and_3_out, and_4_out, and_6_out, and_7_out, and_8_out, B_out,
       button_1_out, C_out, clock_1_out, or_1_out;
  wire [3:0] or_2_out, register_1_q;

  or or_1 (or_1_out, or_2_out[2], or_2_out[1]);
  LED led_1 (.in(or_1_out));
  Clock clock_1 (.out(clock_1_out));
  Button button_1 (.out(button_1_out));
  Register #(.width(4)) register_1 (.D(or_2_out), .Q(register_1_q), .clk(clock_1_out), .clr(button_1_out));  // open: en
  Button A (.out(A_out));
  Button C (.out(C_out));
  Button B (.out(B_out));
  and and_1 (and_1_out, register_1_q[0], A_out);
  and and_2 (and_2_out, register_1_q[1], C_out);
  and and_3 (and_3_out, register_1_q[0], B_out);
  and and_4 (and_4_out, register_1_q[2], C_out);
  and and_5 (or_2_out[3], register_1_q[2], ~C_out);  // AND_Gate
  and and_6 (and_6_out, ~register_1_q[0], ~register_1_q[1], ~register_1_q[2], ~register_1_q[3]);  // AND_Gate
  and and_7 (and_7_out, register_1_q[0], ~C_out, ~B_out, ~A_out);  // AND_Gate
  and and_8 (and_8_out, register_1_q[1], ~C_out);  // AND_Gate
  or or_2 (or_2_out[0], and_2_out, and_6_out, and_7_out, and_4_out);
  or or_3 (or_2_out[2], and_3_out, register_1_q[3]);
  or or_4 (or_2_out[1], and_8_out, and_1_out);
endmodule
